// Logisim project ModularExponent.circ as structural Verilog: 7 circuits, main circuit main
module main (
);

  ModExp modexp_1 ();  // open: Load, Base, Exponent, Modulus, Clock, Result, Result_ready
endmodule

module ModExp (
  input  Load,
  input  [31:0] Base,
  input  [31:0] Exponent,
  input  [15:0] Modulus,
  input  Clock,
  output [31:0] Result,
  output Result_ready
);

  wire clock_1_out, or_1_out;
  wire [31:0] Base_q, Exponent_q, mod_32_1_result, mod_32_2_result, mod_32_3_result, Modulus_q,
       multiplexer_1_out, multiplexer_2_out, multiplexer_3_out, multiplexer_4_out, multiplier_1_out,
       multiplier_2_out, shift1_32_1_result;

  // Probe on Base
  // Probe on Exponent
  // Probe on Modulus
  Multiplexer #(.width(32), .enable("false")) multiplexer_1 (
    .in0(mod_32_2_result), .in1(mod_32_1_result), .out(multiplexer_1_out), .sel(Load));
  Mod_32 mod_32_1 (.Value(Base), .Modulus(Modulus_q), .Result(mod_32_1_result));
  Register #(.width(32)) u_Base (.D(multiplexer_1_out), .Q(Base_q), .clk(clock_1_out));  // open: en, clr
  Multiplexer #(.width(32), .enable("false")) multiplexer_2 (
    .in0(shift1_32_1_result), .in1(Exponent), .out(multiplexer_2_out), .sel(Load));
  Clock clock_1 (.out(clock_1_out));
  Multiplier #(.width(32)) multiplier_1 (.a(Base_q), .b(multiplexer_3_out), .out(multiplier_1_out));  // open: cin, cout
  Multiplexer #(.width(32), .enable("false")) multiplexer_3 (
    .in0(Base_q), .in1(32'h1), .out(multiplexer_3_out));  // open: sel
  Shift1_32 shift1_32_1 (.Value(Exponent_q), .Result(shift1_32_1_result));
  Register #(.width(32)) u_Exponent (.D(multiplexer_2_out), .Q(Exponent_q), .clk(clock_1_out));  // open: en, clr
  Register #(.width(32)) u_Modulus (
    .D({{16{1'b0}}, Modulus}), .en(Load), .Q(Modulus_q), .clk(clock_1_out));  // open: clr
  Mod_32 mod_32_2 (.Value(multiplier_1_out), .Modulus(Modulus_q), .Result(mod_32_2_result));
  Multiplexer #(.width(32), .enable("false")) multiplexer_4 (
    .in0(mod_32_3_result), .in1(32'h1), .out(multiplexer_4_out), .sel(Load));
  or or_1 (or_1_out, Load, Exponent_q[0]);
  IsZero_32 iszero_32_1 (.Value(Exponent_q), .IsZero(Result_ready));
  Register #(.width(32)) u_Result (.D(multiplexer_4_out), .en(or_1_out), .Q(Result), .clk(clock_1_out));  // open: clr
  Multiplier #(.width(32)) multiplier_2 (.a(Base_q), .b(Result), .out(multiplier_2_out));  // open: cin, cout
  Mod_32 mod_32_3 (.Value(multiplier_2_out), .Modulus(Modulus_q), .Result(mod_32_3_result));
  // Probe on Result
endmodule

module Mod_32 (
  input  [31:0] Value,
  input  [31:0] Modulus,
  output [31:0] Result
);

  Divider #(.width(32)) divider_1 (.a(Value), .b(Modulus), .rem(Result));  // open: out, upper
endmodule

module Shift1_32 (
  input  [31:0] Value,
  output [31:0] Result
);

  Shifter #(.width(32), .shift("lr")) shifter_1 (.in(Value), .\dist (5'b00001), .out(Result));
endmodule

module IsZero_32 (
  input  [31:0] Value,
  output IsZero
);

  Comparator #(.width(32)) comparator_1 (.a(Value), .b({32{1'b0}}), .eq(IsZero));  // open: gt, lt
endmodule

module Mult_32 (
  input  [31:0] Value1,
  input  [31:0] Value2,
  output [31:0] Result
);

  Multiplier #(.width(32)) multiplier_1 (.a(Value1), .b(Value2), .out(Result));  // open: cin, cout
endmodule

module MultMod (
  input  [7:0] A,
  input  [7:0] B,
  input  Clk,
  input  [7:0] Modulus,
  output [7:0] P
);

  wire counter_1_carry;
  wire [0:0] register_2_q;
  wire [6:0] register_2_q_2;
  wire [7:0] adder_1_out, and_1_out, bit_extender_1_out, multiplexer_1_out, register_1_q, register_3_q;

  Counter #(.width(3), .max('h7)) counter_1 (
    .load(1'b1), .carry(counter_1_carry), .clk(Clk));  // open: D, count, Q, clr
  Multiplexer #(.width(8), .enable("false")) multiplexer_1 (
    .in0({1'b0, register_2_q_2}), .in1(B), .out(multiplexer_1_out), .sel(counter_1_carry));
  Register register_1 (.D(A), .en(counter_1_carry), .Q(register_1_q));  // open: clk, clr
  Register register_2 (.D(multiplexer_1_out), .Q({register_2_q_2, register_2_q[0]}), .clk(Clk));  // open: en, clr
  assign bit_extender_1_out = {{7{register_2_q[0]}}, register_2_q[0]};  // Bit_Extender bit_extender_1
  assign and_1_out = register_1_q & bit_extender_1_out;  // AND_Gate and_1, 8 bits wide
  Adder adder_1 (.a(register_3_q), .b(and_1_out), .out(adder_1_out));  // open: cin, cout
  Register register_3 (.D(adder_1_out), .Q(register_3_q));  // open: en, clk, clr
endmodule
